# Fritzing sketch schema_arduino (saved by Fritzing 0.9.3b)

parts:
  Composant1 = Arduino Uno (Rev3) - ICSP  # not connected
  Composant2 = Base Shield V2
  Grove_LED_Red1 = Grove LED Red
  Grove_LED_Blue1 = Grove LED Blue
  Grove1 = Grove Button
  Grove_Rotary_Angle_Sensor_(P)1 = Grove Rotary Angle Sensor (P)

nets:
  N1: Composant2.pin_104, Grove1.GND
  N2: Composant2.pin_105, Grove1.VCC
  N3: Composant2.pin_106, Grove1.NC
  N4: Composant2.pin_107, Grove1.SIG
  N5: Composant2.pin_108, Grove_LED_Red1.GND
  N6: Composant2.pin_109, Grove_LED_Red1.NC2
  N7: Composant2.pin_110, Grove_LED_Red1.NC1
  N8: Composant2.pin_111, Grove_LED_Red1.SIG
  N9: Composant2.pin_112, Grove_LED_Blue1.GND
  N10: Composant2.pin_113, Grove_LED_Blue1.NC2
  N11: Composant2.pin_114, Grove_LED_Blue1.NC1
  N12: Composant2.pin_115, Grove_LED_Blue1.SIG
  N13: Composant2.pin_140, Grove_Rotary_Angle_Sensor_(P)1.SIG
  N14: Composant2.pin_141, Grove_Rotary_Angle_Sensor_(P)1.NC
  N15: Composant2.pin_142, Grove_Rotary_Angle_Sensor_(P)1.VCC
  N16: Composant2.pin_143, Grove_Rotary_Angle_Sensor_(P)1.GND

custom parts:
  Grove LED Red: LED red, Grove connector.
  Grove LED Blue: LED blue, Grove connector.
  Grove Rotary Angle Sensor (P): Rotary potentiometer, Grove connector, panel mount.
