# Fritzing sketch shema_arduino (saved by Fritzing 0.9.3b)

parts:
  Composant1 = Arduino Uno (Rev3)  # not connected
  Composant2 = Base Shield V2
  Grove_LED_Blue1 = Grove LED Blue

nets:
  N1: Composant2.pin_104, Grove_LED_Blue1.GND
  N2: Composant2.pin_105, Grove_LED_Blue1.NC2
  N3: Composant2.pin_106, Grove_LED_Blue1.NC1
  N4: Composant2.pin_107, Grove_LED_Blue1.SIG

custom parts:
  Grove LED Blue: LED blue, Grove connector.
