# Fritzing sketch shema_arduino (saved by Fritzing 0.9.3b)

parts:
  Composant1 = Arduino Uno (Rev3)  # not connected
  Composant2 = Base Shield V2
  Grove_LED_Blue2 = Grove LED Blue

nets:
  N1: Composant2.pin_108, Grove_LED_Blue2.GND
  N2: Composant2.pin_109, Grove_LED_Blue2.NC2
  N3: Composant2.pin_110, Grove_LED_Blue2.NC1
  N4: Composant2.pin_111, Grove_LED_Blue2.SIG

custom parts:
  Grove LED Blue: LED blue, Grove connector.
