# Fritzing sketch schema_arduino (saved by Fritzing 0.9.3b)

parts:
  Composant1 = Arduino Uno (Rev3)  # not connected
  Grove_LED_Blue2 = Grove LED Blue
  Composant2 = Base Shield V2

nets:
  N1: Grove_LED_Blue2.SIG, Composant2.pin_99
  N2: Grove_LED_Blue2.NC1, Composant2.pin_98
  N3: Grove_LED_Blue2.NC2, Composant2.pin_97
  N4: Grove_LED_Blue2.GND, Composant2.pin_96

custom parts:
  Grove LED Blue: LED blue, Grove connector.
