# Fritzing sketch schema_arduino (saved by Fritzing 0.9.3b)

parts:
  Composant1 = Arduino Uno (Rev3)  # not connected
  Composant2 = Base Shield V2
  Grove_LED_Blue5 = Grove LED Blue

nets:
  N1: Composant2.pin_96, Grove_LED_Blue5.GND
  N2: Composant2.pin_97, Grove_LED_Blue5.NC2
  N3: Composant2.pin_98, Grove_LED_Blue5.NC1
  N4: Composant2.pin_99, Grove_LED_Blue5.SIG

custom parts:
  Grove LED Blue: LED blue, Grove connector.
