# Fritzing sketch schema_arduino (saved by Fritzing 0.9.3b)

parts:
  Composant1 = Arduino Uno (Rev3)  # not connected
  Composant2 = Base Shield V2
  Grove_LED_Blue3 = Grove LED Blue
  Grove_LED_Blue4 = Grove LED Blue
  Grove_LED_Blue5 = Grove LED Blue
  Grove1 = Grove Rotary Angle Sensor

nets:
  N1: Composant2.pin_104, Grove_LED_Blue4.GND
  N2: Composant2.pin_105, Grove_LED_Blue4.NC2
  N3: Composant2.pin_106, Grove_LED_Blue4.NC1
  N4: Composant2.pin_107, Grove_LED_Blue4.SIG
  N5: Composant2.pin_108, Grove_LED_Blue3.GND
  N6: Composant2.pin_109, Grove_LED_Blue3.NC2
  N7: Composant2.pin_110, Grove_LED_Blue3.NC1
  N8: Composant2.pin_111, Grove_LED_Blue3.SIG
  N9: Composant2.pin_112, Grove_LED_Blue5.GND
  N10: Composant2.pin_113, Grove_LED_Blue5.NC2
  N11: Composant2.pin_114, Grove_LED_Blue5.NC1
  N12: Composant2.pin_115, Grove_LED_Blue5.SIG
  N13: Composant2.pin_140, Grove1.SIG
  N14: Composant2.pin_141, Grove1.NC
  N15: Composant2.pin_142, Grove1.VCC
  N16: Composant2.pin_143, Grove1.GND

custom parts:
  Grove LED Blue: LED blue, Grove connector.
  Grove Rotary Angle Sensor: A potentiometer
