# Fritzing sketch schema_arduino (saved by Fritzing 0.9.3b)

parts:
  Composant1 = Arduino Uno (Rev3)  # not connected
  Composant2 = Base Shield V2
  Grove1 = Grove Temperature Sensor
  Grove2 = Grove OLED 128x96

nets:
  N1: Composant2.pin_100, Grove1.GND
  N2: Composant2.pin_101, Grove1.VCC
  N3: Composant2.pin_103, Grove1.SIG
  N4: Composant2.pin_124, Grove2.GND
  N5: Composant2.pin_125, Grove2.VCC
  N6: Composant2.pin_126, Grove2.SDA
  N7: Composant2.pin_127, Grove2.SCL
